# Fritzing sketch 4_sinusschakeling (saved by Fritzing 0.9.9b)
breadboards: 1

parts:
  Part1 = Arduino Nano (Rev3.0)
  C1 = Ceramic Capacitor [capacitance=2.2µF voltage=35V package="100 mil [THT, multilayer]"]
  R1 = Resistor [tolerance=±5% power=0.25 resistance=100 package=THT]
  R2 = Resistor [tolerance=±5% power=0.25 resistance=1k package=THT]
  C2 = Electrolytic Capacitor [capacitance=100nF voltage=35V package="100 mil [THT, electrolytic]"]
  R3 = Rotary Potentiometer (Large) [maximum_resistance=10kΩ package=THT]

nets:
  N1: Part1.D9, C1.1
  N2: C1.0, R1.Pin_1, R2.Pin_0
  N3: R1.Pin_0, C2.+, R3.leg2
  N4: R2.Pin_1, C2.-, R3.leg1

custom parts:
  Arduino Nano (Rev3.0): The Arduino Nano is a small, complete, and breadboard-friendly board based on the ATmega328 (Arduino Nano 3.0) or ATmega168 (Arduino Nano 2.x). It has more or less the same functionality of the Arduino Duemilanove, but in a different package. It lacks only a DC power jack, and works with a Mini-B USB cable instead of a standard one. The Nano was designed and is being produced by Gravitech.
